# Fritzing sketch Wiring (saved by Fritzing 0.9.3b)
breadboards: 1

parts:
  Part1 = Arduino Mega ADK (Rev3)
  J1 = Basic Servo  # not connected
  J2 = Basic Servo  # not connected
  J3 = Basic Servo  # not connected
  J4 = Basic Servo  # not connected
  J5 = Basic Servo  # not connected
  Part2 = 16-Channel 12-bit PWM Servo Driver - I2C [part_number=815]

nets:
  N1: Part1.D21/SCL, Part2.SCL
  N2: Part1.D20/SDA, Part2.SDA

custom parts:
  16-Channel 12-bit PWM Servo Driver - I2C: You want to make a cool robot, maybe a hexapod walker, or maybe just a piece of art with a lot of moving parts. Or maybe you want to drive a lot of LEDs with precise PWM output. Using only two pins, control 16 free-running PWM outputs! You can even chain up 62 breakouts to control up to 992 PWM outputs.
